# Fritzing sketch Diseño del circuito (saved by Fritzing 0.9.3b)
breadboards: 1

parts:
  U1 = ESP32-30Pin [part_number=ESP32-30Pin]
  J1 = Piezo Speaker
  Componente1 = MQ-4

nets:
  VIN: U1.VIN, Componente1.VCC
  N1: U1.GND#1, Componente1.GND
  N2: U1.D27, Componente1.AO
  N3: U1.3v3, J1.pin2
  N4: U1.GND#16, J1.pin1

custom parts:
  ESP32-30Pin: Generic 30-Pin ESP32
